# Fritzing sketch tension (saved by Fritzing 0.9.3b)
circuit board: 8.46667cm x 5.64444cm

parts:
  Raspberry_Pi_1 = Raspberry Pi 3 [part_number=RPI-3-V1.2]
  Grove1 = Grove OLED 128x96
  D1 = LED_BARGRAPH_10 [package=led_bargaph_10]
  Grove2 = Grove OLED 128x96
  U1 = 74HC4051 [package=so16]  # not connected
  U2 = cd4021 [package=so16]  # not connected
  S1 = Round Pushbutton
  U3 = 74HC595 [package="DIP16 [THT]"]
  R1 = Resistor [tolerance=±5% resistance=220 package=THT]
  R2 = Resistor [tolerance=±5% resistance=220 package=THT]
  R3 = Resistor [tolerance=±5% resistance=220 package=THT]
  R4 = Resistor [tolerance=±5% resistance=220 package=THT]
  R5 = Resistor [tolerance=±5% resistance=220 package=THT]
  R6 = Resistor [tolerance=±5% resistance=220 package=THT]
  R7 = Resistor [tolerance=±5% resistance=220 package=THT]
  R10 = Resistor [tolerance=±5% resistance=220 package=THT]
  LED8 = LED - 3mm [color="Red (633nm)" package="3 mm [THT]"]
  LED9 = LED - 3mm [color="Red (633nm)" package="3 mm [THT]"]
  LED10 = LED - 3mm [color="Red (633nm)" package="3 mm [THT]"]
  LED11 = LED - 3mm [color="Red (633nm)" package="3 mm [THT]"]
  LED12 = LED - 3mm [color="Red (633nm)" package="3 mm [THT]"]
  LED13 = LED - 3mm [color="Red (633nm)" package="3 mm [THT]"]
  LED14 = LED - 3mm [color="Red (633nm)" package="3 mm [THT]"]
  LED15 = LED - 3mm [color="Red (633nm)" package="3 mm [THT]"]
  U4 = 74HC595 [package="DIP16 [THT]"]
  LED16 = LED - 3mm [color="Red (633nm)" package="3 mm [THT]"]
  LED17 = LED - 3mm [color="Red (633nm)" package="3 mm [THT]"]
  LED18 = LED - 3mm [color="Red (633nm)" package="3 mm [THT]"]
  LED19 = LED - 3mm [color="Red (633nm)" package="3 mm [THT]"]
  LED20 = LED - 3mm [color="Red (633nm)" package="3 mm [THT]"]
  LED21 = LED - 3mm [color="Red (633nm)" package="3 mm [THT]"]
  LED22 = LED - 3mm [color="Red (633nm)" package="3 mm [THT]"]
  LED23 = LED - 3mm [color="Red (633nm)" package="3 mm [THT]"]
  R11 = Resistor [tolerance=±5% resistance=220 package=THT]
  R12 = Resistor [tolerance=±5% resistance=220 package=THT]
  R13 = Resistor [tolerance=±5% resistance=220 package=THT]
  R14 = Resistor [tolerance=±5% resistance=220 package=THT]
  R15 = Resistor [tolerance=±5% resistance=220 package=THT]
  R16 = Resistor [tolerance=±5% resistance=220 package=THT]
  R17 = Resistor [tolerance=±5% resistance=220 package=THT]
  R18 = Resistor [tolerance=±5% resistance=220 package=THT]
  U5 = 74HC595 [package="DIP16 [THT]"]
  LED24 = LED - 3mm [color="Red (633nm)" package="3 mm [THT]"]
  LED25 = LED - 3mm [color="Red (633nm)" package="3 mm [THT]"]
  LED26 = LED - 3mm [color="Red (633nm)" package="3 mm [THT]"]
  LED27 = LED - 3mm [color="Red (633nm)" package="3 mm [THT]"]
  LED28 = LED - 3mm [color="Red (633nm)" package="3 mm [THT]"]
  LED29 = LED - 3mm [color="Red (633nm)" package="3 mm [THT]"]
  LED30 = LED - 3mm [color="Red (633nm)" package="3 mm [THT]"]
  LED31 = LED - 3mm [color="Red (633nm)" package="3 mm [THT]"]
  R19 = Resistor [tolerance=±5% resistance=220 package=THT]
  R20 = Resistor [tolerance=±5% resistance=220 package=THT]
  R21 = Resistor [tolerance=±5% resistance=220 package=THT]
  R22 = Resistor [tolerance=±5% resistance=220 package=THT]
  R23 = Resistor [tolerance=±5% resistance=220 package=THT]
  R24 = Resistor [tolerance=±5% resistance=220 package=THT]
  R25 = Resistor [tolerance=±5% resistance=220 package=THT]
  R26 = Resistor [tolerance=±5% resistance=220 package=THT]
  U6 = 74HC595 [package="DIP16 [THT]"]
  LED32 = LED - 3mm [color="Red (633nm)" package="3 mm [THT]"]
  LED33 = LED - 3mm [color="Red (633nm)" package="3 mm [THT]"]
  LED34 = LED - 3mm [color="Red (633nm)" package="3 mm [THT]"]
  LED35 = LED - 3mm [color="Red (633nm)" package="3 mm [THT]"]
  LED36 = LED - 3mm [color="Red (633nm)" package="3 mm [THT]"]
  LED37 = LED - 3mm [color="Red (633nm)" package="3 mm [THT]"]
  LED38 = LED - 3mm [color="Red (633nm)" package="3 mm [THT]"]
  LED39 = LED - 3mm [color="Red (633nm)" package="3 mm [THT]"]
  R27 = Resistor [tolerance=±5% resistance=220 package=THT]
  R28 = Resistor [tolerance=±5% resistance=220 package=THT]
  R29 = Resistor [tolerance=±5% resistance=220 package=THT]
  R30 = Resistor [tolerance=±5% resistance=220 package=THT]
  R31 = Resistor [tolerance=±5% resistance=220 package=THT]
  R32 = Resistor [tolerance=±5% resistance=220 package=THT]
  R33 = Resistor [tolerance=±5% resistance=220 package=THT]
  R34 = Resistor [tolerance=±5% resistance=220 package=THT]
  U7 = 74HC595 [package="DIP16 [THT]"]
  LED40 = LED - 3mm [color="Red (633nm)" package="3 mm [THT]"]
  LED41 = LED - 3mm [color="Red (633nm)" package="3 mm [THT]"]
  LED42 = LED - 3mm [color="Red (633nm)" package="3 mm [THT]"]
  LED43 = LED - 3mm [color="Red (633nm)" package="3 mm [THT]"]
  LED44 = LED - 3mm [color="Red (633nm)" package="3 mm [THT]"]
  LED45 = LED - 3mm [color="Red (633nm)" package="3 mm [THT]"]
  LED46 = LED - 3mm [color="Red (633nm)" package="3 mm [THT]"]
  LED47 = LED - 3mm [color="Red (633nm)" package="3 mm [THT]"]
  R35 = Resistor [tolerance=±5% resistance=220 package=THT]
  R36 = Resistor [tolerance=±5% resistance=220 package=THT]
  R37 = Resistor [tolerance=±5% resistance=220 package=THT]
  R38 = Resistor [tolerance=±5% resistance=220 package=THT]
  R39 = Resistor [tolerance=±5% resistance=220 package=THT]
  R40 = Resistor [tolerance=±5% resistance=220 package=THT]
  R41 = Resistor [tolerance=±5% resistance=220 package=THT]
  R42 = Resistor [tolerance=±5% resistance=220 package=THT]
  U8 = 74HC595 [package="DIP16 [THT]"]
  LED48 = LED - 3mm [color="Red (633nm)" package="3 mm [THT]"]
  LED49 = LED - 3mm [color="Red (633nm)" package="3 mm [THT]"]
  LED50 = LED - 3mm [color="Red (633nm)" package="3 mm [THT]"]
  LED51 = LED - 3mm [color="Red (633nm)" package="3 mm [THT]"]
  LED52 = LED - 3mm [color="Red (633nm)" package="3 mm [THT]"]
  LED53 = LED - 3mm [color="Red (633nm)" package="3 mm [THT]"]
  LED54 = LED - 3mm [color="Red (633nm)" package="3 mm [THT]"]
  LED55 = LED - 3mm [color="Red (633nm)" package="3 mm [THT]"]
  R43 = Resistor [tolerance=±5% resistance=220 package=THT]
  R44 = Resistor [tolerance=±5% resistance=220 package=THT]
  R45 = Resistor [tolerance=±5% resistance=220 package=THT]
  R46 = Resistor [tolerance=±5% resistance=220 package=THT]
  R47 = Resistor [tolerance=±5% resistance=220 package=THT]
  R48 = Resistor [tolerance=±5% resistance=220 package=THT]
  R49 = Resistor [tolerance=±5% resistance=220 package=THT]
  R50 = Resistor [tolerance=±5% resistance=220 package=THT]
  U9 = 74HC595 [package="DIP16 [THT]"]
  LED56 = LED - 3mm [color="Red (633nm)" package="3 mm [THT]"]
  LED57 = LED - 3mm [color="Red (633nm)" package="3 mm [THT]"]
  LED58 = LED - 3mm [color="Red (633nm)" package="3 mm [THT]"]
  LED59 = LED - 3mm [color="Red (633nm)" package="3 mm [THT]"]
  LED60 = LED - 3mm [color="Red (633nm)" package="3 mm [THT]"]
  LED61 = LED - 3mm [color="Red (633nm)" package="3 mm [THT]"]
  LED62 = LED - 3mm [color="Red (633nm)" package="3 mm [THT]"]
  LED63 = LED - 3mm [color="Red (633nm)" package="3 mm [THT]"]
  R51 = Resistor [tolerance=±5% resistance=220 package=THT]
  R52 = Resistor [tolerance=±5% resistance=220 package=THT]
  R53 = Resistor [tolerance=±5% resistance=220 package=THT]
  R54 = Resistor [tolerance=±5% resistance=220 package=THT]
  R55 = Resistor [tolerance=±5% resistance=220 package=THT]
  R56 = Resistor [tolerance=±5% resistance=220 package=THT]
  R57 = Resistor [tolerance=±5% resistance=220 package=THT]
  R58 = Resistor [tolerance=±5% resistance=220 package=THT]
  U10 = 74HC595 [package="DIP16 [THT]"]
  LED64 = LED - 3mm [color="Red (633nm)" package="3 mm [THT]"]
  LED65 = LED - 3mm [color="Red (633nm)" package="3 mm [THT]"]
  LED66 = LED - 3mm [color="Red (633nm)" package="3 mm [THT]"]
  LED67 = LED - 3mm [color="Red (633nm)" package="3 mm [THT]"]
  LED68 = LED - 3mm [color="Red (633nm)" package="3 mm [THT]"]
  LED69 = LED - 3mm [color="Red (633nm)" package="3 mm [THT]"]
  LED70 = LED - 3mm [color="Red (633nm)" package="3 mm [THT]"]
  LED71 = LED - 3mm [color="Red (633nm)" package="3 mm [THT]"]
  R59 = Resistor [tolerance=±5% resistance=220 package=THT]
  R60 = Resistor [tolerance=±5% resistance=220 package=THT]
  R61 = Resistor [tolerance=±5% resistance=220 package=THT]
  R62 = Resistor [tolerance=±5% resistance=220 package=THT]
  R63 = Resistor [tolerance=±5% resistance=220 package=THT]
  R64 = Resistor [tolerance=±5% resistance=220 package=THT]
  R65 = Resistor [tolerance=±5% resistance=220 package=THT]
  R66 = Resistor [tolerance=±5% resistance=220 package=THT]
  U11 = 74HC595 [package="DIP16 [THT]"]
  Grove3 = Grove OLED 128x96  # not connected
  U12 = 74HC595 [package="DIP16 [THT]"]
  Grove4 = Grove OLED 128x96  # not connected
  Grove5 = Grove OLED 128x96  # not connected
  Grove6 = Grove OLED 128x96  # not connected
  S2 = Round Pushbutton
  Grove7 = Grove OLED 128x96  # not connected
  Grove8 = Grove OLED 128x96  # not connected
  Grove9 = Grove OLED 128x96  # not connected
  Grove10 = Grove OLED 128x96  # not connected
  Grove11 = Grove OLED 128x96  # not connected
  Grove12 = Grove OLED 128x96  # not connected
  U13 = 74HC595 [package="DIP16 [THT]"]
  R67 = Resistor [tolerance=±5% resistance=220 package=THT]
  R68 = Resistor [tolerance=±5% resistance=220 package=THT]
  R69 = Resistor [tolerance=±5% resistance=220 package=THT]
  R70 = Resistor [tolerance=±5% resistance=220 package=THT]
  R71 = Resistor [tolerance=±5% resistance=220 package=THT]
  R72 = Resistor [tolerance=±5% resistance=220 package=THT]
  R73 = Resistor [tolerance=±5% resistance=220 package=THT]
  R74 = Resistor [tolerance=±5% resistance=220 package=THT]
  D2 = LED_BARGRAPH_10 [package=led_bargaph_10]
  U14 = 74HC595 [package="DIP16 [THT]"]
  R75 = Resistor [tolerance=±5% resistance=220 package=THT]
  R76 = Resistor [tolerance=±5% resistance=220 package=THT]
  R77 = Resistor [tolerance=±5% resistance=220 package=THT]
  R78 = Resistor [tolerance=±5% resistance=220 package=THT]
  R79 = Resistor [tolerance=±5% resistance=220 package=THT]
  R80 = Resistor [tolerance=±5% resistance=220 package=THT]
  R81 = Resistor [tolerance=±5% resistance=220 package=THT]
  R82 = Resistor [tolerance=±5% resistance=220 package=THT]
  U15 = 74HC595 [package="DIP16 [THT]"]
  R83 = Resistor [tolerance=±5% resistance=220 package=THT]
  R84 = Resistor [tolerance=±5% resistance=220 package=THT]
  R85 = Resistor [tolerance=±5% resistance=220 package=THT]
  R86 = Resistor [tolerance=±5% resistance=220 package=THT]
  R87 = Resistor [tolerance=±5% resistance=220 package=THT]
  R88 = Resistor [tolerance=±5% resistance=220 package=THT]
  R89 = Resistor [tolerance=±5% resistance=220 package=THT]
  R90 = Resistor [tolerance=±5% resistance=220 package=THT]
  D3 = LED_BARGRAPH_10 [package=led_bargaph_10]
  U16 = 74HC595 [package="DIP16 [THT]"]
  R91 = Resistor [tolerance=±5% resistance=220 package=THT]
  R92 = Resistor [tolerance=±5% resistance=220 package=THT]
  R93 = Resistor [tolerance=±5% resistance=220 package=THT]
  R94 = Resistor [tolerance=±5% resistance=220 package=THT]
  R95 = Resistor [tolerance=±5% resistance=220 package=THT]
  R96 = Resistor [tolerance=±5% resistance=220 package=THT]
  R97 = Resistor [tolerance=±5% resistance=220 package=THT]
  R98 = Resistor [tolerance=±5% resistance=220 package=THT]
  U17 = 74HC595 [package="DIP16 [THT]"]
  R99 = Resistor [tolerance=±5% resistance=220 package=THT]
  R100 = Resistor [tolerance=±5% resistance=220 package=THT]
  R101 = Resistor [tolerance=±5% resistance=220 package=THT]
  R102 = Resistor [tolerance=±5% resistance=220 package=THT]
  R103 = Resistor [tolerance=±5% resistance=220 package=THT]
  R104 = Resistor [tolerance=±5% resistance=220 package=THT]
  R105 = Resistor [tolerance=±5% resistance=220 package=THT]
  R106 = Resistor [tolerance=±5% resistance=220 package=THT]
  U18 = 74HC595 [package="DIP16 [THT]"]
  R107 = Resistor [tolerance=±5% resistance=220 package=THT]
  R108 = Resistor [tolerance=±5% resistance=220 package=THT]
  R109 = Resistor [tolerance=±5% resistance=220 package=THT]
  R110 = Resistor [tolerance=±5% resistance=220 package=THT]
  R111 = Resistor [tolerance=±5% resistance=220 package=THT]
  R112 = Resistor [tolerance=±5% resistance=220 package=THT]
  R113 = Resistor [tolerance=±5% resistance=220 package=THT]
  R114 = Resistor [tolerance=±5% resistance=220 package=THT]
  U19 = 74HC595 [package="DIP16 [THT]"]
  R115 = Resistor [tolerance=±5% resistance=220 package=THT]
  R116 = Resistor [tolerance=±5% resistance=220 package=THT]
  R117 = Resistor [tolerance=±5% resistance=220 package=THT]
  R118 = Resistor [tolerance=±5% resistance=220 package=THT]
  R119 = Resistor [tolerance=±5% resistance=220 package=THT]
  R120 = Resistor [tolerance=±5% resistance=220 package=THT]
  R121 = Resistor [tolerance=±5% resistance=220 package=THT]
  R122 = Resistor [tolerance=±5% resistance=220 package=THT]
  U20 = 74HC595 [package="DIP16 [THT]"]
  R123 = Resistor [tolerance=±5% resistance=220 package=THT]
  R124 = Resistor [tolerance=±5% resistance=220 package=THT]
  R125 = Resistor [tolerance=±5% resistance=220 package=THT]
  R126 = Resistor [tolerance=±5% resistance=220 package=THT]
  R127 = Resistor [tolerance=±5% resistance=220 package=THT]
  R128 = Resistor [tolerance=±5% resistance=220 package=THT]
  R129 = Resistor [tolerance=±5% resistance=220 package=THT]
  R130 = Resistor [tolerance=±5% resistance=220 package=THT]
  U21 = 74HC595 [package="DIP16 [THT]"]
  U22 = 74HC595 [package="DIP16 [THT]"]
  U23 = 74HC595 [package="DIP16 [THT]"]
  U24 = 74HC595 [package="DIP16 [THT]"]
  U25 = 74HC595 [package="DIP16 [THT]"]
  U26 = 74HC595 [package="DIP16 [THT]"]
  U27 = 74HC595 [package="DIP16 [THT]"]
  R131 = Resistor [tolerance=±5% resistance=220 package=THT]
  R132 = Resistor [tolerance=±5% resistance=220 package=THT]
  R133 = Resistor [tolerance=±5% resistance=220 package=THT]
  R134 = Resistor [tolerance=±5% resistance=220 package=THT]
  R135 = Resistor [tolerance=±5% resistance=220 package=THT]
  R136 = Resistor [tolerance=±5% resistance=220 package=THT]
  R137 = Resistor [tolerance=±5% resistance=220 package=THT]
  R138 = Resistor [tolerance=±5% resistance=220 package=THT]
  R139 = Resistor [tolerance=±5% resistance=220 package=THT]
  R140 = Resistor [tolerance=±5% resistance=220 package=THT]
  R141 = Resistor [tolerance=±5% resistance=220 package=THT]
  R142 = Resistor [tolerance=±5% resistance=220 package=THT]
  R143 = Resistor [tolerance=±5% resistance=220 package=THT]
  R144 = Resistor [tolerance=±5% resistance=220 package=THT]
  R145 = Resistor [tolerance=±5% resistance=220 package=THT]
  R146 = Resistor [tolerance=±5% resistance=220 package=THT]
  R147 = Resistor [tolerance=±5% resistance=220 package=THT]
  R148 = Resistor [tolerance=±5% resistance=220 package=THT]
  R149 = Resistor [tolerance=±5% resistance=220 package=THT]
  R150 = Resistor [tolerance=±5% resistance=220 package=THT]
  R151 = Resistor [tolerance=±5% resistance=220 package=THT]
  R152 = Resistor [tolerance=±5% resistance=220 package=THT]
  R153 = Resistor [tolerance=±5% resistance=220 package=THT]
  R154 = Resistor [tolerance=±5% resistance=220 package=THT]
  R155 = Resistor [tolerance=±5% resistance=220 package=THT]
  R156 = Resistor [tolerance=±5% resistance=220 package=THT]
  R157 = Resistor [tolerance=±5% resistance=220 package=THT]
  R158 = Resistor [tolerance=±5% resistance=220 package=THT]
  R159 = Resistor [tolerance=±5% resistance=220 package=THT]
  R160 = Resistor [tolerance=±5% resistance=220 package=THT]
  R161 = Resistor [tolerance=±5% resistance=220 package=THT]
  R162 = Resistor [tolerance=±5% resistance=220 package=THT]
  R163 = Resistor [tolerance=±5% resistance=220 package=THT]
  R164 = Resistor [tolerance=±5% resistance=220 package=THT]
  R165 = Resistor [tolerance=±5% resistance=220 package=THT]
  R166 = Resistor [tolerance=±5% resistance=220 package=THT]
  R167 = Resistor [tolerance=±5% resistance=220 package=THT]
  R168 = Resistor [tolerance=±5% resistance=220 package=THT]
  R169 = Resistor [tolerance=±5% resistance=220 package=THT]
  R170 = Resistor [tolerance=±5% resistance=220 package=THT]
  R171 = Resistor [tolerance=±5% resistance=220 package=THT]
  R172 = Resistor [tolerance=±5% resistance=220 package=THT]
  R173 = Resistor [tolerance=±5% resistance=220 package=THT]
  R174 = Resistor [tolerance=±5% resistance=220 package=THT]
  R175 = Resistor [tolerance=±5% resistance=220 package=THT]
  R176 = Resistor [tolerance=±5% resistance=220 package=THT]
  R177 = Resistor [tolerance=±5% resistance=220 package=THT]
  R178 = Resistor [tolerance=±5% resistance=220 package=THT]
  R179 = Resistor [tolerance=±5% resistance=220 package=THT]
  R180 = Resistor [tolerance=±5% resistance=220 package=THT]
  R181 = Resistor [tolerance=±5% resistance=220 package=THT]
  R182 = Resistor [tolerance=±5% resistance=220 package=THT]
  R183 = Resistor [tolerance=±5% resistance=220 package=THT]
  R184 = Resistor [tolerance=±5% resistance=220 package=THT]
  R185 = Resistor [tolerance=±5% resistance=220 package=THT]
  R186 = Resistor [tolerance=±5% resistance=220 package=THT]
  D4 = LED_BARGRAPH_10 [package=led_bargaph_10]
  D5 = LED_BARGRAPH_10 [package=led_bargaph_10]
  D6 = LED_BARGRAPH_10 [package=led_bargaph_10]
  D7 = LED_BARGRAPH_10 [package=led_bargaph_10]
  D8 = LED_BARGRAPH_10 [package=led_bargaph_10]
  D9 = LED_BARGRAPH_10 [package=led_bargaph_10]
  D10 = LED_BARGRAPH_10 [package=led_bargaph_10]
  D11 = LED_BARGRAPH_10 [package=led_bargaph_10]
  D12 = LED_BARGRAPH_10 [package=led_bargaph_10]
  R187 = Resistor [tolerance=±5% resistance=220 package=THT]
  R188 = Resistor [tolerance=±5% resistance=220 package=THT]
  R189 = Resistor [tolerance=±5% resistance=220 package=THT]
  S3 = Round Pushbutton
  R190 = Resistor [tolerance=±5% resistance=220 package=THT]
  U28 = Voltage Regulator - 5V [package="TO220 [THT]"]  # not connected

nets:
  N1: Raspberry_Pi_1.GPIO2, Grove1.SDA, Grove2.SDA
  N2: Raspberry_Pi_1.GPIO3, Grove1.SCL, Grove2.SCL
  GND: Raspberry_Pi_1.GND, Grove1.GND, Grove2.GND
  VCC: Raspberry_Pi_1.5V, Grove1.VCC, Grove2.VCC
  N3: D1.A_A, R77.Pin_1
  N4: D1.B_A, R81.Pin_1
  N5: D1.C_A, R67.Pin_1
  N6: D1.D_A, R71.Pin_1
  N7: D1.E_A, R70.Pin_1
  N8: D1.F_A, R72.Pin_1
  N9: D1.G_A, R73.Pin_1
  N10: D1.H_A, R74.Pin_1
  N11: D1.I_A, R68.Pin_1
  N12: D1.J_A, R69.Pin_1
  N13: S1.leg0, R188.Pin_1
  N14: U3.Q1, R7.Pin_0
  N15: U3.Q2, R6.Pin_0
  N16: U3.Q3, R5.Pin_0
  N17: U3.Q4, R4.Pin_0
  N18: U3.Q5, R3.Pin_0
  N19: U3.Q6, R2.Pin_0
  N20: U3.Q7, R1.Pin_0
  N21: U3.GND, U3.OE, LED8.cathode, LED9.cathode, LED10.cathode, LED11.cathode, LED12.cathode, LED13.cathode, LED14.cathode, LED15.cathode
  N22: U3.Q7', U4.DS
  N23: U3.MR, U3.VCC
  N24: U3.SH_CP, U4.SH_CP, U5.SH_CP, U6.SH_CP, U7.SH_CP, U8.SH_CP, U9.SH_CP, U10.SH_CP
  N25: U3.ST_CP, U4.ST_CP, U5.ST_CP, U6.ST_CP, U7.ST_CP, U8.ST_CP, U9.ST_CP, U10.ST_CP
  N26: U3.Q0, R10.Pin_0
  N27: R1.Pin_1, LED12.anode
  N28: R2.Pin_1, LED13.anode
  N29: R3.Pin_1, LED14.anode
  N30: R4.Pin_1, LED15.anode
  N31: R5.Pin_1, LED10.anode
  N32: R6.Pin_1, LED11.anode
  N33: R7.Pin_1, LED9.anode
  N34: R10.Pin_1, LED8.anode
  N35: U4.Q1, R13.Pin_0
  N36: U4.Q2, R17.Pin_0
  N37: U4.Q3, R14.Pin_0
  N38: U4.Q4, R15.Pin_0
  N39: U4.Q5, R16.Pin_0
  N40: U4.Q6, R18.Pin_0
  N41: U4.Q7, R11.Pin_0
  N42: U4.GND, U4.OE, LED16.cathode, LED17.cathode, LED18.cathode, LED19.cathode, LED20.cathode, LED21.cathode, LED22.cathode, LED23.cathode
  N43: U4.Q7', U6.DS
  N44: U4.MR, U4.VCC
  N45: U4.Q0, R12.Pin_0
  N46: LED16.anode, R17.Pin_1
  N47: LED17.anode, R12.Pin_1
  N48: LED18.anode, R11.Pin_1
  N49: LED19.anode, R14.Pin_1
  N50: LED20.anode, R16.Pin_1
  N51: LED21.anode, R18.Pin_1
  N52: LED22.anode, R13.Pin_1
  N53: LED23.anode, R15.Pin_1
  N54: U5.Q1, R19.Pin_0
  N55: U5.Q2, R22.Pin_0
  N56: U5.Q3, R21.Pin_0
  N57: U5.Q4, R20.Pin_0
  N58: U5.Q5, R25.Pin_0
  N59: U5.Q6, R24.Pin_0
  N60: U5.Q7, R23.Pin_0
  N61: U5.GND, U5.OE, LED24.cathode, LED25.cathode, LED26.cathode, LED27.cathode, LED28.cathode, LED29.cathode, LED30.cathode, LED31.cathode
  N62: U5.MR, U5.VCC
  N63: U5.DS, U10.Q7'
  N64: U5.Q0, R26.Pin_0
  N65: LED24.anode, R25.Pin_1
  N66: LED25.anode, R24.Pin_1
  N67: LED26.anode, R21.Pin_1
  N68: LED27.anode, R19.Pin_1
  N69: LED28.anode, R22.Pin_1
  N70: LED29.anode, R23.Pin_1
  N71: LED30.anode, R20.Pin_1
  N72: LED31.anode, R26.Pin_1
  N73: U6.Q1, R30.Pin_0
  N74: U6.Q2, R27.Pin_0
  N75: U6.Q3, R28.Pin_0
  N76: U6.Q4, R33.Pin_0
  N77: U6.Q5, R29.Pin_0
  N78: U6.Q6, R31.Pin_0
  N79: U6.Q7, R32.Pin_0
  N80: U6.GND, U6.OE, LED32.cathode, LED33.cathode, LED34.cathode, LED35.cathode, LED36.cathode, LED37.cathode, LED38.cathode, LED39.cathode
  N81: U6.Q7', U7.DS
  N82: U6.MR, U6.VCC
  N83: U6.Q0, R34.Pin_0
  N84: LED32.anode, R31.Pin_1
  N85: LED33.anode, R29.Pin_1
  N86: LED34.anode, R28.Pin_1
  N87: LED35.anode, R30.Pin_1
  N88: LED36.anode, R33.Pin_1
  N89: LED37.anode, R34.Pin_1
  N90: LED38.anode, R32.Pin_1
  N91: LED39.anode, R27.Pin_1
  N92: U7.Q1, R38.Pin_0
  N93: U7.Q2, R35.Pin_0
  N94: U7.Q3, R36.Pin_0
  N95: U7.Q4, R41.Pin_0
  N96: U7.Q5, R37.Pin_0
  N97: U7.Q6, R39.Pin_0
  N98: U7.Q7, R40.Pin_0
  N99: U7.GND, U7.OE, LED40.cathode, LED41.cathode, LED42.cathode, LED43.cathode, LED44.cathode, LED45.cathode, LED46.cathode, LED47.cathode
  N100: U7.Q7', U8.DS
  N101: U7.MR, U7.VCC
  N102: U7.Q0, R42.Pin_0
  N103: LED40.anode, R39.Pin_1
  N104: LED41.anode, R37.Pin_1
  N105: LED42.anode, R36.Pin_1
  N106: LED43.anode, R38.Pin_1
  N107: LED44.anode, R41.Pin_1
  N108: LED45.anode, R42.Pin_1
  N109: LED46.anode, R40.Pin_1
  N110: LED47.anode, R35.Pin_1
  N111: U8.Q1, R46.Pin_0
  N112: U8.Q2, R43.Pin_0
  N113: U8.Q3, R44.Pin_0
  N114: U8.Q4, R49.Pin_0
  N115: U8.Q5, R45.Pin_0
  N116: U8.Q6, R47.Pin_0
  N117: U8.Q7, R48.Pin_0
  N118: U8.GND, U8.OE, LED48.cathode, LED49.cathode, LED50.cathode, LED51.cathode, LED52.cathode, LED53.cathode, LED54.cathode, LED55.cathode
  N119: U8.Q7', U9.DS
  N120: U8.MR, U8.VCC
  N121: U8.Q0, R50.Pin_0
  N122: LED48.anode, R47.Pin_1
  N123: LED49.anode, R45.Pin_1
  N124: LED50.anode, R44.Pin_1
  N125: LED51.anode, R46.Pin_1
  N126: LED52.anode, R49.Pin_1
  N127: LED53.anode, R50.Pin_1
  N128: LED54.anode, R48.Pin_1
  N129: LED55.anode, R43.Pin_1
  N130: U9.Q1, R54.Pin_0
  N131: U9.Q2, R51.Pin_0
  N132: U9.Q3, R52.Pin_0
  N133: U9.Q4, R57.Pin_0
  N134: U9.Q5, R53.Pin_0
  N135: U9.Q6, R55.Pin_0
  N136: U9.Q7, R56.Pin_0
  N137: U9.GND, U9.OE, LED56.cathode, LED57.cathode, LED58.cathode, LED59.cathode, LED60.cathode, LED61.cathode, LED62.cathode, LED63.cathode
  N138: U9.Q7', U10.DS
  N139: U9.MR, U9.VCC
  N140: U9.Q0, R58.Pin_0
  N141: LED56.anode, R55.Pin_1
  N142: LED57.anode, R53.Pin_1
  N143: LED58.anode, R52.Pin_1
  N144: LED59.anode, R54.Pin_1
  N145: LED60.anode, R57.Pin_1
  N146: LED61.anode, R58.Pin_1
  N147: LED62.anode, R56.Pin_1
  N148: LED63.anode, R51.Pin_1
  N149: U10.Q1, R62.Pin_0
  N150: U10.Q2, R59.Pin_0
  N151: U10.Q3, R60.Pin_0
  N152: U10.Q4, R65.Pin_0
  N153: U10.Q5, R61.Pin_0
  N154: U10.Q6, R63.Pin_0
  N155: U10.Q7, R64.Pin_0
  N156: U10.GND, U10.OE, LED64.cathode, LED65.cathode, LED66.cathode, LED67.cathode, LED68.cathode, LED69.cathode, LED70.cathode, LED71.cathode
  N157: U10.MR, U10.VCC
  N158: U10.Q0, R66.Pin_0
  N159: LED64.anode, R63.Pin_1
  N160: LED65.anode, R61.Pin_1
  N161: LED66.anode, R60.Pin_1
  N162: LED67.anode, R62.Pin_1
  N163: LED68.anode, R65.Pin_1
  N164: LED69.anode, R66.Pin_1
  N165: LED70.anode, R64.Pin_1
  N166: LED71.anode, R59.Pin_1
  N167: U11.GND, U11.OE
  N168: U11.Q7', U12.DS
  N169: U11.MR, U11.VCC
  N170: U11.SH_CP, U12.SH_CP
  N171: U11.ST_CP, U12.ST_CP
  N172: U12.GND, U12.OE
  N173: U12.MR, U12.VCC
  N174: S2.leg0, R189.Pin_1
  N175: U13.Q1, R68.Pin_0
  N176: U13.Q2, R74.Pin_0
  N177: U13.Q3, R73.Pin_0
  N178: U13.Q4, R72.Pin_0
  N179: U13.Q5, R70.Pin_0
  N180: U13.Q6, R71.Pin_0
  N181: U13.Q7, R67.Pin_0
  N182: U13.GND, U13.OE
  N183: U13.Q7', U14.DS
  N184: U13.MR, U13.VCC
  N185: U13.SH_CP, U14.SH_CP, U15.SH_CP, U16.SH_CP, U17.SH_CP, U18.SH_CP, U19.SH_CP, U20.SH_CP, U21.SH_CP, U22.SH_CP, U23.SH_CP, U24.SH_CP, U25.SH_CP, U26.SH_CP, U27.SH_CP
  N186: U13.ST_CP, U14.ST_CP, U15.ST_CP, U16.ST_CP, U17.ST_CP, U18.ST_CP, U19.ST_CP, U20.ST_CP, U21.ST_CP, U22.ST_CP, U23.ST_CP, U24.ST_CP, U25.ST_CP, U26.ST_CP, U27.ST_CP
  N187: U13.Q0, R69.Pin_0
  N188: D2.A_A, R84.Pin_1
  N189: D2.B_A, R88.Pin_1
  N190: D2.C_A, R85.Pin_1
  N191: D2.D_A, R87.Pin_1
  N192: D2.E_A, R80.Pin_1
  N193: D2.F_A, R76.Pin_1
  N194: D2.G_A, R82.Pin_1
  N195: D2.H_A, R78.Pin_1
  N196: D2.I_A, R75.Pin_1
  N197: D2.J_A, R79.Pin_1
  N198: U14.Q1, R77.Pin_0
  N199: U14.Q2, R79.Pin_0
  N200: U14.Q3, R75.Pin_0
  N201: U14.Q4, R78.Pin_0
  N202: U14.Q5, R82.Pin_0
  N203: U14.Q6, R76.Pin_0
  N204: U14.Q7, R80.Pin_0
  N205: U14.GND, U14.OE
  N206: U14.Q7', U15.DS
  N207: U14.MR, U14.VCC
  N208: U14.Q0, R81.Pin_0
  N209: U15.Q1, R85.Pin_0
  N210: U15.Q2, R88.Pin_0
  N211: U15.Q3, R84.Pin_0
  N212: U15.Q4, R83.Pin_0
  N213: U15.Q5, R86.Pin_0
  N214: U15.Q6, R90.Pin_0
  N215: U15.Q7, R89.Pin_0
  N216: U15.GND, U15.OE
  N217: U15.Q7', U16.DS
  N218: U15.MR, U15.VCC
  N219: U15.Q0, R87.Pin_0
  N220: R83.Pin_1, D3.J_A
  N221: R86.Pin_1, D3.I_A
  N222: R89.Pin_1, D3.G_A
  N223: R90.Pin_1, D3.H_A
  N224: D3.A_A, R98.Pin_1
  N225: D3.B_A, R92.Pin_1
  N226: D3.C_A, R96.Pin_1
  N227: D3.D_A, R95.Pin_1
  N228: D3.E_A, R91.Pin_1
  N229: D3.F_A, R97.Pin_1
  N230: U16.Q1, R91.Pin_0
  N231: U16.Q2, R95.Pin_0
  N232: U16.Q3, R96.Pin_0
  N233: U16.Q4, R92.Pin_0
  N234: U16.Q5, R98.Pin_0
  N235: U16.Q6, R94.Pin_0
  N236: U16.Q7, R93.Pin_0
  N237: U16.GND, U16.OE
  N238: U16.Q7', U17.DS
  N239: U16.MR, U16.VCC
  N240: U16.Q0, R97.Pin_0
  N241: R93.Pin_1, D4.I_A
  N242: R94.Pin_1, D4.J_A
  N243: U17.Q1, R99.Pin_0
  N244: U17.Q2, R103.Pin_0
  N245: U17.Q3, R104.Pin_0
  N246: U17.Q4, R100.Pin_0
  N247: U17.Q5, R106.Pin_0
  N248: U17.Q6, R102.Pin_0
  N249: U17.Q7, R101.Pin_0
  N250: U17.GND, U17.OE
  N251: U17.Q7', U18.DS
  N252: U17.MR, U17.VCC
  N253: U17.Q0, R105.Pin_0
  N254: R99.Pin_1, D4.G_A
  N255: R100.Pin_1, D4.D_A
  N256: R101.Pin_1, D4.A_A
  N257: R102.Pin_1, D4.B_A
  N258: R103.Pin_1, D4.F_A
  N259: R104.Pin_1, D4.E_A
  N260: R105.Pin_1, D4.H_A
  N261: R106.Pin_1, D4.C_A
  N262: U18.Q1, R107.Pin_0
  N263: U18.Q2, R111.Pin_0
  N264: U18.Q3, R112.Pin_0
  N265: U18.Q4, R108.Pin_0
  N266: U18.Q5, R114.Pin_0
  N267: U18.Q6, R110.Pin_0
  N268: U18.Q7, R109.Pin_0
  N269: U18.GND, U18.OE
  N270: U18.Q7', U19.DS
  N271: U18.MR, U18.VCC
  N272: U18.Q0, R113.Pin_0
  N273: R107.Pin_1, D5.I_A
  N274: R108.Pin_1, D5.F_A
  N275: R109.Pin_1, D5.C_A
  N276: R110.Pin_1, D5.D_A
  N277: R111.Pin_1, D5.H_A
  N278: R112.Pin_1, D5.G_A
  N279: R113.Pin_1, D5.J_A
  N280: R114.Pin_1, D5.E_A
  N281: U19.Q1, R115.Pin_0
  N282: U19.Q2, R119.Pin_0
  N283: U19.Q3, R120.Pin_0
  N284: U19.Q4, R116.Pin_0
  N285: U19.Q5, R122.Pin_0
  N286: U19.Q6, R118.Pin_0
  N287: U19.Q7, R117.Pin_0
  N288: U19.GND, U19.OE
  N289: U19.Q7', U20.DS
  N290: U19.MR, U19.VCC
  N291: U19.Q0, R121.Pin_0
  N292: R115.Pin_1, D5.A_A
  N293: R116.Pin_1, D6.H_A
  N294: R117.Pin_1, D6.E_A
  N295: R118.Pin_1, D6.F_A
  N296: R119.Pin_1, D6.J_A
  N297: R120.Pin_1, D6.I_A
  N298: R121.Pin_1, D5.B_A
  N299: R122.Pin_1, D6.G_A
  N300: U20.Q1, R123.Pin_0
  N301: U20.Q2, R127.Pin_0
  N302: U20.Q3, R128.Pin_0
  N303: U20.Q4, R124.Pin_0
  N304: U20.Q5, R130.Pin_0
  N305: U20.Q6, R126.Pin_0
  N306: U20.Q7, R125.Pin_0
  N307: U20.GND, U20.OE
  N308: U20.Q7', U26.DS
  N309: U20.MR, U20.VCC
  N310: U20.Q0, R129.Pin_0
  N311: R123.Pin_1, D6.C_A
  N312: R124.Pin_1, D7.J_A
  N313: R125.Pin_1, D7.G_A
  N314: R126.Pin_1, D7.H_A
  N315: R127.Pin_1, D6.B_A
  N316: R128.Pin_1, D6.A_A
  N317: R129.Pin_1, D6.D_A
  N318: R130.Pin_1, D7.I_A
  N319: U21.Q1, R177.Pin_0
  N320: U21.Q2, R173.Pin_0
  N321: U21.Q3, R176.Pin_0
  N322: U21.Q4, R184.Pin_0
  N323: U21.Q5, R162.Pin_0
  N324: U21.Q6, R151.Pin_0
  N325: U21.Q7, R157.Pin_0
  N326: U21.GND, U21.OE
  N327: U21.Q7', U27.DS
  N328: U21.MR, U21.VCC
  N329: U21.DS, U25.Q7'
  N330: U21.Q0, R164.Pin_0
  N331: U22.Q1, R134.Pin_0
  N332: U22.Q2, R143.Pin_0
  N333: U22.Q3, R185.Pin_0
  N334: U22.Q4, R167.Pin_0
  N335: U22.Q5, R153.Pin_0
  N336: U22.Q6, R180.Pin_0
  N337: U22.Q7, R149.Pin_0
  N338: U22.GND, U22.OE
  N339: U22.Q7', U23.DS
  N340: U22.MR, U22.VCC
  N341: U22.DS, U27.Q7'
  N342: U22.Q0, R168.Pin_0
  N343: U23.Q1, R181.Pin_0
  N344: U23.Q2, R182.Pin_0
  N345: U23.Q3, R142.Pin_0
  N346: U23.Q4, R175.Pin_0
  N347: U23.Q5, R137.Pin_0
  N348: U23.Q6, R174.Pin_0
  N349: U23.Q7, R156.Pin_0
  N350: U23.GND, U23.OE
  N351: U23.MR, U23.VCC
  N352: U23.Q0, R132.Pin_0
  N353: U24.Q1, R145.Pin_0
  N354: U24.Q2, R131.Pin_0
  N355: U24.Q3, R138.Pin_0
  N356: U24.Q4, R135.Pin_0
  N357: U24.Q5, R183.Pin_0
  N358: U24.Q6, R158.Pin_0
  N359: U24.Q7, R155.Pin_0
  N360: U24.GND, U24.OE
  N361: U24.Q7', U25.DS
  N362: U24.MR, U24.VCC
  N363: U24.DS, U26.Q7'
  N364: U24.Q0, R178.Pin_0
  N365: U25.Q1, R165.Pin_0
  N366: U25.Q2, R136.Pin_0
  N367: U25.Q3, R133.Pin_0
  N368: U25.Q4, R186.Pin_0
  N369: U25.Q5, R150.Pin_0
  N370: U25.Q6, R171.Pin_0
  N371: U25.Q7, R154.Pin_0
  N372: U25.GND, U25.OE
  N373: U25.MR, U25.VCC
  N374: U25.Q0, R141.Pin_0
  N375: U26.Q1, R147.Pin_0
  N376: U26.Q2, R148.Pin_0
  N377: U26.Q3, R179.Pin_0
  N378: U26.Q4, R166.Pin_0
  N379: U26.Q5, R152.Pin_0
  N380: U26.Q6, R161.Pin_0
  N381: U26.Q7, R169.Pin_0
  N382: U26.GND, U26.OE
  N383: U26.MR, U26.VCC
  N384: U26.Q0, R163.Pin_0
  N385: U27.Q1, R160.Pin_0
  N386: U27.Q2, R146.Pin_0
  N387: U27.Q3, R139.Pin_0
  N388: U27.Q4, R172.Pin_0
  N389: U27.Q5, R170.Pin_0
  N390: U27.Q6, R159.Pin_0
  N391: U27.Q7, R140.Pin_0
  N392: U27.GND, U27.OE
  N393: U27.MR, U27.VCC
  N394: U27.Q0, R144.Pin_0
  N395: R131.Pin_1, D8.F_A
  N396: R132.Pin_1, D10.H_A
  N397: R133.Pin_1, D9.G_A
  N398: R134.Pin_1, D11.E_A
  N399: R135.Pin_1, D8.D_A
  N400: R136.Pin_1, D9.H_A
  N401: R137.Pin_1, D10.C_A
  N402: R138.Pin_1, D8.E_A
  N403: R139.Pin_1, D12.A_A
  N404: R140.Pin_1, D11.G_A
  N405: R141.Pin_1, D9.J_A
  N406: R142.Pin_1, D10.E_A
  N407: R143.Pin_1, D11.D_A
  N408: R144.Pin_1, D12.D_A
  N409: R145.Pin_1, D8.G_A
  N410: R146.Pin_1, D12.B_A
  N411: R147.Pin_1, D7.E_A
  N412: R148.Pin_1, D7.D_A
  N413: R149.Pin_1, D10.I_A
  N414: R150.Pin_1, D9.E_A
  N415: R151.Pin_1, D12.F_A
  N416: R152.Pin_1, D7.A_A
  N417: R153.Pin_1, D11.A_A
  N418: R154.Pin_1, D9.C_A
  N419: R155.Pin_1, D8.A_A
  N420: R156.Pin_1, D10.A_A
  N421: R157.Pin_1, D12.E_A
  N422: R158.Pin_1, D8.B_A
  N423: R159.Pin_1, D11.H_A
  N424: R160.Pin_1, D12.C_A
  N425: R161.Pin_1, D8.J_A
  N426: R162.Pin_1, D12.G_A
  N427: R163.Pin_1, D7.F_A
  N428: R164.Pin_1, D9.B_A
  N429: R165.Pin_1, D9.I_A
  N430: R166.Pin_1, D7.B_A
  N431: R167.Pin_1, D11.B_A
  N432: R168.Pin_1, D11.F_A
  N433: R169.Pin_1, D8.I_A
  N434: R170.Pin_1, D11.I_A
  N435: R171.Pin_1, D9.D_A
  N436: R172.Pin_1, D11.J_A
  N437: R173.Pin_1, D12.J_A
  N438: R174.Pin_1, D10.B_A
  N439: R175.Pin_1, D10.D_A
  N440: R176.Pin_1, D12.I_A
  N441: R177.Pin_1, D9.A_A
  N442: R178.Pin_1, D8.H_A
  N443: R179.Pin_1, D7.C_A
  N444: R180.Pin_1, D10.J_A
  N445: R181.Pin_1, D10.G_A
  N446: R182.Pin_1, D10.F_A
  N447: R183.Pin_1, D8.C_A
  N448: R184.Pin_1, D12.H_A
  N449: R185.Pin_1, D11.C_A
  N450: R186.Pin_1, D9.F_A
  N451: R187.Pin_1, R189.Pin_0, R190.Pin_0
  N452: S3.leg0, R190.Pin_1

custom parts:
  cd4021: 8:1 parallel to serial register
